# Fritzing sketch ESP8266_Kanji_Clock (saved by Fritzing 0.9.3b)

parts:
  0x70 = 8x8 LED Matrix (red)
  0x72 = 8x8 LED Matrix (red)
  0x71 = 8x8 LED Matrix (red)
  0x73 = 8x8 LED Matrix (red)
  JACK1 = 2.1mm DC Barrel Jack
  S1 = Toggle Switch [package=THT]
  Part2 = Adafruit HUZZAH ESP8266 [part_number="Adafruit #2471"]

nets:
  N1: 0x70.+, 0x72.+, 0x71.+, 0x73.+, Part2.3.3V
  N2: 0x70.-, 0x72.-, 0x71.-, 0x73.-, JACK1.sleeve, Part2.GND
  N3: 0x70.D, 0x72.D, 0x71.D, 0x73.D, Part2.GPIO4
  N4: 0x70.C, 0x72.C, 0x71.C, 0x73.C, Part2.GPIO5
  N5: JACK1.center, Part2.VIN
  N6: S1.L1, Part2.GPIO12
  N7: S1.COM, Part2.GPIO14
  N8: S1.L2, Part2.GPIO16

custom parts:
  8x8 LED Matrix (red): 8x8 LED Matrix with I2C control (red)
  2.1mm DC Barrel Jack: 2.1mm DC Barrel Jack with Thru-Hole Connectors (breadboardable)
  Adafruit HUZZAH ESP8266: Add Internet to your next project with an adorable, bite-sized WiFi microcontroller, at a price you like! The ESP8266 processor from Espressif is an 80 MHz microcontroller with a full WiFi front-end (both as client and access point) and TCP/IP stack with DNS support as well. While this chip has been very popular, its also been very difficult to use. Most of the low cost modules are not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
